# Fritzing sketch esp8266-wiring (saved by Fritzing 0.9.3b)
breadboards: 1

parts:
  U1 = ESP8266 WiFi Module [part_number=ESP8266]
  U8 = POT [package=pot_mammoth]
  J6 = JST-03JQ-BT [part_number=JST-JQ-BT package=THT]
  J7 = JST-03JQ-BT [part_number=JST-JQ-BT package=THT]
  J8 = JST-03JQ-BT [part_number=JST-JQ-BT package=THT]
  J9 = JST-03JQ-BT [part_number=JST-JQ-BT package=THT]
  U9 = Optocoupler [package=THT]
  U10 = LIPO-2000mAh [package=lipo-2000]
  R1 = Resistor [tolerance=±5% resistance=220 package=THT]

nets:
  N1: U1.GND#13, R1.Pin_1
  N2: U1.IO13, U9.Pin_2
  N3: U1.GND#23, U10.-
  N4: U1.3.3V#26, U10.+
  N5: U8.S, J7.pin1, J8.pin1, U9.Pin_5
  N6: U8.A, J6.pin2, J7.pin2, J8.pin2, J9.pin2
  N7: U8.E, J6.pin3, J7.pin3, J8.pin3, J9.pin3
  N8: J6.pin1, J9.pin1, U9.Pin_4
  N9: U9.Pin_1, R1.Pin_0

notes:
  Scooter Head Unit
  Scooter Throttle
